// Logisim project HW1.circ as structural Verilog: 1 circuit, main circuit main
module main (
  input  S1,
  input  S1_2,
  input  S2,
  input  S2_2,
  input  S3,
  input  S3_2,
  input  S4,
  input  S4_2,
  input  S1_3,
  input  in_10,
  input  S2_3,
  input  in_12,
  input  in_13,
  input  S4_3,
  input  S1_4,
  input  S1_5,
  input  S2_4,
  input  S2_5,
  input  in_19,
  input  S3_3,
  input  S4_4,
  input  S4_5,
  output Y,
  output Y_2,
  output out_25,
  output Y_3,
  output out_27,
  output out_28
);

  wire and_1_out, and_2_out, and_3_out, and_4_out, and_5_out, and_6_out, and_7_out, and_8_out, and_9_out,
       and_10_out, and_12_out, and_13_out, and_14_out, and_15_out, and_17_out, and_18_out, and_19_out,
       and_20_out, nand_1_out, nor_1_out, nor_2_out, not_1_out, not_2_out, not_3_out, not_4_out, not_5_out,
       not_6_out, not_7_out, not_8_out, not_9_out, not_10_out, not_11_out, not_12_out, not_13_out, or_1_out,
       or_2_out, or_3_out, or_4_out, or_5_out, or_6_out, or_7_out, or_8_out, or_10_out, or_11_out, or_13_out,
       or_14_out;

  not not_1 (not_1_out, in_19);
  not not_2 (not_2_out, S1);
  not not_3 (not_3_out, S2);
  not not_4 (not_4_out, S3);
  not not_5 (not_5_out, S4_2);
  and and_1 (and_1_out, S1_4, S2_4);
  nand nand_1 (nand_1_out, S1_4, S2_4);
  and and_2 (and_2_out, not_2_out, S2);
  and and_3 (and_3_out, S1, not_3_out);
  and and_4 (and_4_out, not_4_out, S4_2);
  and and_5 (and_5_out, S3, not_5_out);
  or or_1 (or_1_out, S1_3, S2_3);
  and and_6 (and_6_out, S1_3, S2_3);
  not not_6 (not_6_out, and_6_out);
  or or_2 (or_2_out, in_13, S4_3);
  and and_7 (and_7_out, in_13, S4_3);
  not not_7 (not_7_out, and_7_out);
  or or_3 (or_3_out, and_2_out, and_3_out);
  or or_4 (or_4_out, and_4_out, and_5_out);
  and and_8 (and_8_out, or_1_out, not_6_out);
  and and_9 (and_9_out, or_2_out, not_7_out);
  or or_5 (or_5_out, and_1_out, not_1_out);
  and and_10 (and_10_out, S4_4, nand_1_out);
  nor nor_1 (nor_1_out, S4_4, in_19);
  or or_6 (or_6_out, S1_4, S2_4);
  // AND_Gate and_11 is placed but not wired
  not not_8 (not_8_out, or_3_out);
  not not_9 (not_9_out, or_4_out);
  and and_12 (and_12_out, or_5_out, and_10_out);
  or or_7 (or_7_out, nor_1_out, or_6_out);
  and and_13 (and_13_out, not_8_out, or_4_out);
  and and_14 (and_14_out, or_3_out, not_9_out);
  or or_8 (or_8_out, and_8_out, and_9_out);
  and and_15 (and_15_out, and_8_out, and_9_out);
  not not_10 (not_10_out, and_15_out);
  nand nand_2 (out_27, and_12_out, or_7_out);
  or or_9 (Y, and_13_out, and_14_out);
  and and_16 (Y_3, or_8_out, not_10_out);
  // RGB_Video #(.height(64), .scale(3), .width(64)) rgb_video_1: pin names not known; wires that end beside it: S1_2, S2_2, S4, S3_2, Y_2, out_25
  and and_17 (and_17_out, in_10, in_12);
  nor nor_2 (nor_2_out, in_10, in_12);
  or or_10 (or_10_out, S1_5, S2_5);
  and and_18 (and_18_out, S2_5, S1_5);
  or or_11 (or_11_out, S3_3, S4_5);
  not not_11 (not_11_out, and_18_out);
  not not_12 (not_12_out, or_11_out);
  not not_13 (not_13_out, S3_3);
  or or_12 (out_25, and_17_out, nor_2_out);
  and and_19 (and_19_out, or_10_out, not_11_out);
  and and_20 (and_20_out, not_13_out, S4_5);
  or or_13 (or_13_out, and_19_out, not_12_out);
  or or_14 (or_14_out, and_18_out, and_20_out);
  and and_21 (out_28, or_13_out, or_14_out);

  // Notes on the sheet:
  //   S3
  //   S3
  //   Logical Design HW-1
  //   Method 1: XOR = a'b+a b'
  //   Method 2 XOR = (a+b)(a b)'
  //   Total: 12
  //   412770116 許嘉隆 AI-2B
  //   Total: 15
  //   2-inputs AND * 6
  //   2-inputs OR * 3
  //   1-inputs NOT * 3
  //   2-inputs AND * 6
  //   2-inputs OR * 3
  //   1-inputs NOT * 6
  //   輸入閘(S1,S2,S3,S4)和輸出閘(Y)個數圖
  //   Test1
endmodule
