// Logisim project test.circ as structural Verilog: 1 circuit, main circuit main
module main (
  input  S1,
  input  S2,
  input  S3,
  input  S4,
  output Y
);

  wire and_1_out, and_2_out, and_3_out, and_4_out, and_5_out, and_6_out, not_1_out, not_2_out, not_3_out,
       not_4_out, not_5_out, not_6_out, or_1_out, or_2_out;

  not not_1 (not_1_out, S1);
  not not_2 (not_2_out, S2);
  not not_3 (not_3_out, S3);
  not not_4 (not_4_out, S4);
  and and_1 (and_1_out, not_1_out, not_1_out, S2);
  and and_2 (and_2_out, S1, not_2_out);
  and and_3 (and_3_out, not_3_out, not_3_out, S4);
  and and_4 (and_4_out, S3, not_4_out);
  or or_1 (or_1_out, and_1_out, and_2_out);
  or or_2 (or_2_out, and_3_out, and_4_out);
  not not_5 (not_5_out, or_1_out);
  not not_6 (not_6_out, or_2_out);
  and and_5 (and_5_out, not_5_out, not_5_out, or_2_out);
  and and_6 (and_6_out, or_1_out, not_6_out);
  or or_3 (Y, and_5_out, and_6_out);

  // Notes on the sheet:
  //   412770116 許嘉隆 AI-2B
  //   Logical Design HW-1
  //   2-inputs AND * 6
  //   2-inputs OR * 3
  //   1-inputs NOT * 6
  //   Total: 15
endmodule
